# Fritzing sketch stove_arduino_fritzing_v1.0.0 (saved by Fritzing 0.9.10b)

parts:
  Servo = Dagu DGServo 9g (Top view) [part_number=RS001B]
  9V_in_5V_out = DC-DC_CONVERTER [package=dc-dc_converter]
  MAX6675_Temp_Sensor = MAX6675 [package=so08]
  Part1 = Arduino Uno (Rev3) - ICSP
  K-Type_Thermocouple_(d-ring) = nozzle-bolt style thermocouple [package=THT]
  LCD_16x2 = LCD-16X2 [package=lcd-16x2_nosilk]
  LCD_Brightness = POT [knob_status=50% power=0.5W package=pot_alpha_rv16af-20]
  Mode/Temp_Setting = POT [knob_status=50% power=0.5W package=pot_alpha_rv16af-20]
  Buzzer = Piezo Speaker
  R1 = Resistor [tolerance=±5% resistance=1k package="1206 [SMD]"]
  9V_3A = Power plug

nets:
  GND: Servo.gnd, 9V_in_5V_out.GND2
  N1: Servo.vcc, 9V_in_5V_out.VOUT
  N2: Servo.pulse, Part1.D10_PWM/SS
  VIN: 9V_in_5V_out.VIN, 9V_3A.VCC
  GND1: 9V_in_5V_out.GND1, 9V_3A.GND
  VSS: MAX6675_Temp_Sensor.VSS, Part1.GND, LCD_16x2.VSS, LCD_16x2.R_W, LCD_16x2.K, LCD_Brightness.A, Mode/Temp_Setting.A, Buzzer.pin1
  N3: MAX6675_Temp_Sensor.T-, K-Type_Thermocouple_(d-ring).pin2
  N4: MAX6675_Temp_Sensor.T+, K-Type_Thermocouple_(d-ring).pin1
  VDD: MAX6675_Temp_Sensor.VDD, Part1.5V
  N5: MAX6675_Temp_Sensor.SCK, Part1.D8
  N6: MAX6675_Temp_Sensor.CS, Part1.D6_PWM
  N7: MAX6675_Temp_Sensor.MISO, Part1.D7
  N8: Part1.A2, Mode/Temp_Setting.S
  N9: Part1.ICSP_MISO, Part1.D12/MISO, LCD_16x2.RS
  N10: Part1.ICSP_MOSI, Part1.D11_PWM/MOSI, LCD_16x2.E
  N11: Part1.D9_PWM, R1.Pin_1
  N12: Part1.D2, LCD_16x2.DB7
  N13: Part1.D3_PWM, LCD_16x2.DB6
  N14: Part1.D4, LCD_16x2.DB5
  N15: Part1.D5_PWM, LCD_16x2.DB4
  N16: LCD_16x2.VDD, Mode/Temp_Setting.E
  N17: LCD_16x2.VO, LCD_Brightness.S
  N18: LCD_16x2.A, LCD_Brightness.E
  N19: Buzzer.pin2, R1.Pin_0

custom parts:
  nozzle-bolt style thermocouple: Generic nozzle-bolt style thermocouple.
