# Fritzing sketch stove_arduino_fritzing_v3 (saved by Fritzing 0.9.10b)

parts:
  Servo = Dagu DGServo 9g (Top view) [part_number=RS001B]
  9V_in_5V_out = DC-DC_CONVERTER [package=dc-dc_converter]
  MAX6675_Temp_Sensor = MAX6675 [package=so08]
  Part1 = Arduino Uno (Rev3) - ICSP
  K-Type_Thermocouple_(d-ring) = nozzle-bolt style thermocouple [package=THT]
  Temporary_Mock_Temp = POT [knob_status=50% power=0.5W package=pot_alpha_rv16af-20]
  Buzzer = Piezo Speaker
  R1 = Resistor [tolerance=±5% resistance=1k package="1206 [SMD]"]
  9V_3A = Power plug
  Part2 = Nextion LCD DRAFT [part_number=Nextion]

nets:
  GND: Servo.gnd, 9V_in_5V_out.GND2, Part2.GND
  VCC: Servo.vcc, 9V_in_5V_out.VOUT, Part2.VCC
  N1: Servo.pulse, Part1.D10_PWM/SS
  VIN: 9V_in_5V_out.VIN, 9V_3A.VCC
  GND1: 9V_in_5V_out.GND1, 9V_3A.GND
  VSS: MAX6675_Temp_Sensor.VSS, Part1.GND, Temporary_Mock_Temp.A, Buzzer.pin1
  N2: MAX6675_Temp_Sensor.T-, K-Type_Thermocouple_(d-ring).pin2
  N3: MAX6675_Temp_Sensor.T+, K-Type_Thermocouple_(d-ring).pin1
  VDD: MAX6675_Temp_Sensor.VDD, Part1.5V, Temporary_Mock_Temp.E
  N4: MAX6675_Temp_Sensor.SCK, Part1.D8
  N5: MAX6675_Temp_Sensor.CS, Part1.D6_PWM
  N6: MAX6675_Temp_Sensor.MISO, Part1.D7
  N7: Part1.A2, Temporary_Mock_Temp.S
  N8: Part1.D9_PWM, R1.Pin_1
  N9: Part1.D0/RX, Part2.Tx
  N10: Part1.D1/TX, Part2.Rx
  N11: Buzzer.pin2, R1.Pin_0

custom parts:
  nozzle-bolt style thermocouple: Generic nozzle-bolt style thermocouple.
  Nextion LCD DRAFT: Nextion HMI 2.4" TFT 320x240 resistive Lcd touch screen Intelligent Display Module for Arduino NX3224T024 4M Flash, 2KByte RAM, 65k colors
